// Logisim project A2_Group3.circ as structural Verilog: 3 circuits, main circuit xi_yi
module xi_yi (
  input  m0,
  input  m5,
  input  ai,
  input  ai_prime,
  input  bi,
  input  bi_prime,
  input  s2,
  input  s1,
  input  s0,
  input  s0_prime,
  output yi,
  output xi
);

  wire n7408_1_p4, n7408_1_p7, n7408_1_p12, n7408_1_p14, n7408_1_p15, n7432_1_p6;

  // _7408 7408_1: pin names not known; wires that end beside it: 1'b0, bi_prime, m0, n7408_1_p4, bi, m5, n7408_1_p7, 1'b0, 1'b1, s0_prime, bi, n7408_1_p12, ai, n7408_1_p14, n7408_1_p15
  // _7432 7432_1: pin names not known; wires that end beside it: n7408_1_p7, n7408_1_p4, yi, ai, bi, n7432_1_p6, 1'b0, 1'b1, n7408_1_p12, s0, n7408_1_p14
  // _74153 74153_1: pin names not known; wires that end beside it: 1'b0, s2, n7432_1_p6, n7408_1_p15, ai_prime, ai, xi, 1'b0, 1'b1, s1

  // Notes on the sheet:
  //   bim5
  //   bi' mo
  //   ai + bi
  //   s0' bi
  //   ai(s0' bi + s0)
  //   ai
  //   s0' bi + s0
  //   s0
endmodule

module main (
  input  a3,
  input  a2,
  input  a1,
  input  a0,
  input  b3,
  input  b2,
  input  b1,
  input  b0,
  input  s2,
  input  s1,
  input  s0,
  output Cout,
  output O3,
  output O2,
  output O1,
  output O0,
  output C,
  output Z,
  output V,
  output S
);

  wire n7404_1_p2, n7404_1_p4, n7404_1_p8, n7404_1_p10, n7404_2_p1, n7404_2_p4, n7404_2_p7, n7404_2_p10,
       n7404_2_p12, n7404_2_p14, n7432_1_p2, n7432_1_p3, n7432_1_p6, n74238_1_p1, n74238_1_p11, n74238_1_p12,
       n74238_1_p13, n74238_1_p14, n74238_1_p15, n74238_1_p16, n74238_1_p17, xi_yi_1_xi, xi_yi_1_yi,
       xi_yi_2_xi, xi_yi_2_yi, xi_yi_3_xi, xi_yi_3_yi, xi_yi_4_xi, xi_yi_4_yi;

  // _7404 7404_1: pin names not known; wires that end beside it: a1, n7404_1_p2, a2, n7404_1_p4, a3, 1'b1, a0, n7404_1_p8, b3, n7404_1_p10
  // _7404 7404_2: pin names not known; wires that end beside it: n7404_2_p1, 1'b0, s2, n7404_2_p4, 1'b0, b2, n7404_2_p7, 1'b1, b1, n7404_2_p10, b0, n7404_2_p12, s0, n7404_2_p14
  // _74238 74238_1: pin names not known; wires that end beside it: n74238_1_p1, s0, s1, s2, 1'b0, 1'b0, 1'b1, n74238_1_p1, 1'b0, 1'b1, n74238_1_p11, n74238_1_p12, n74238_1_p13, n74238_1_p14, n74238_1_p15, n74238_1_p16, n74238_1_p17, n74238_1_p12, n74238_1_p13, n74238_1_p14, n74238_1_p15, n74238_1_p17
  xi_yi xi_yi_1 (
    .m0(n74238_1_p11), .m5(n74238_1_p16), .ai(a3), .ai_prime(n7404_2_p1), .bi(b3), .bi_prime(n7404_1_p10),
    .s2(s2), .s1(s1), .s0(s0), .s0_prime(n7404_2_p14), .yi(xi_yi_1_yi), .xi(xi_yi_1_xi));
  xi_yi xi_yi_2 (
    .m0(n74238_1_p11), .m5(n74238_1_p16), .ai(a2), .ai_prime(n7404_1_p4), .bi(b2), .bi_prime(n7404_2_p7),
    .s2(s2), .s1(s1), .s0(s0), .s0_prime(n7404_2_p14), .yi(xi_yi_2_yi), .xi(xi_yi_2_xi));
  xi_yi xi_yi_3 (
    .m0(n74238_1_p11), .m5(n74238_1_p16), .ai(a1), .ai_prime(n7404_1_p2), .bi(b1), .bi_prime(n7404_2_p10),
    .s2(s2), .s1(s1), .s0(s0), .s0_prime(n7404_2_p14), .yi(xi_yi_3_yi), .xi(xi_yi_3_xi));
  xi_yi xi_yi_4 (
    .m0(n74238_1_p11), .m5(n74238_1_p16), .ai(a0), .ai_prime(n7404_1_p8), .bi(b0), .bi_prime(n7404_2_p12),
    .s2(s2), .s1(s1), .s0(s0), .s0_prime(n7404_2_p14), .yi(xi_yi_4_yi), .xi(xi_yi_4_xi));
  // _7432 7432_1: pin names not known; wires that end beside it: n74238_1_p16, n7432_1_p2, n7432_1_p3, s1, n7404_2_p14, n7432_1_p6, 1'b0, 1'b1
  // _7408 7408_1: pin names not known; wires that end beside it: n7404_2_p4, n7432_1_p6, n7432_1_p2, 1'b0, 1'b1
  // _7483 7483_1: pin names not known; wires that end beside it: xi_yi_1_xi, O2, xi_yi_2_xi, xi_yi_2_yi, 1'b1, O1, xi_yi_3_yi, xi_yi_3_xi, xi_yi_1_yi, O3, Cout, n7432_1_p3, 1'b0, xi_yi_4_yi, xi_yi_4_xi, O0
  flag flag_1 (
    .O3(O3), .O2(O2), .O1(O1), .O0(O0), .x3(xi_yi_1_xi), .y3(xi_yi_1_yi), .Cout(Cout), .C(C), .Z(Z), .V(V),
    .S(S));

  // Notes on the sheet:
  //   a2
  //   a3
  //   a2
  //   a3
  //   a2
  //   a3
  //   a2
  //   a3
  //   a2
  //   a3
  //   a1
  //   a0
  //   b2
  //   b3
  //   a1
  //   b2
  //   b3
  //   a0
  //   a1
  //   b2
  //   a0
  //   b3
  //   a1
  //   a0
  //   b3
  //   b2
  //   a1
  //   a0
  //   b2
  //   b3
  //   b0
  //   b1
  //   s2
  //   s1
  //   b1
  //   b0
  //   s2
  //   s1
  //   b1
  //   s2
  //   b0
  //   s1
  //   b1
  //   b0
  //   s2
  //   s1
  //   s2
  //   b1
  //   b0
  //   s1
  //   s0
  //   NOT
  //   s0
  //   s0
  //   s0
  //   s0
  //   a3'
  //   a1'
  //   a2'
  //   s0'
  //   a3'
  //   a2'
  //   a1'
  //   s0'
  //   a3'
  //   a1'
  //   a2'
  //   s0'
  //   a3'
  //   a2'
  //   a1'
  //   a3'
  //   s0'
  //   a2'
  //   a1'
  //   a0'
  //   b3'
  //   b2'
  //   b1'
  //   a0'
  //   b3'
  //   b1'
  //   b2'
  //   a0'
  //   b3'
  //   b1'
  //   b2'
  //   a0'
  //   b2'
  //   b1'
  //   b3'
  //   a0'
  //   b3'
  //   b2'
  //   b1'
  //   s2
  //   s0
  //   s1
  //   b0'
  //   b0'
  //   b0'
  //   b0'
  //   b0'
  //   m5
  //   m5
  //   Decoder
  //   m0
  //   m0
  //   m0
  //   m0
  //   m0
  //   m5
  //   s0'
  //   y3
  //   x3
  //   y2
  //   x2
  //   y1
  //   x1
  //   y0
  //   x0
  //   s2'
  //   OR
  //   AND
  //   4bit full adder
  //   Cin
endmodule

module flag (
  input  O3,
  input  O2,
  input  O1,
  input  O0,
  input  x3,
  input  y3,
  input  Cout,
  output C,
  output Z,
  output V,
  output S
);

  wire n7432_1_p3, n7432_1_p6, n7432_1_p11, n7486_1_p3, n7486_1_p6;

  // _7432 7432_1: pin names not known; wires that end beside it: O0, O1, n7432_1_p3, n7432_1_p3, O2, n7432_1_p6, 1'b0, 1'b1, n7432_1_p6, O3, n7432_1_p11
  // _7486 7486_1: pin names not known; wires that end beside it: Cout, y3, n7486_1_p3, n7486_1_p3, x3, n7486_1_p6, 1'b0, 1'b1, 1'b1, n7432_1_p11, Z, n7486_1_p6, O3, V

  assign C = Cout;
  assign S = O3;
endmodule
