// Logisim project A2_Group3.circ as structural Verilog: 11 circuits, main circuit Exponent Compare
module Exponent_Compare (
  input  [11:0] A,
  input  [11:0] B,
  output K,
  output S,
  output [11:0] N,
  output S_prime,
  output [4:0] M
);

  wire comparator_2_gt;
  wire [11:0] multiplexer_2_out, subtractor_1_out;

  Comparator #(.width(12), .mode("unsigned")) comparator_1 (.a(A), .b(B), .gt(K), .eq(S), .lt(S_prime));
  Multiplexer #(.width(12), .enable("false")) multiplexer_1 (.in0(B), .in1(A), .out(N), .sel(K));
  Multiplexer #(.width(12), .enable("false")) multiplexer_2 (.in0(A), .in1(B), .out(multiplexer_2_out), .sel(K));
  Comparator #(.width(12), .mode("unsigned")) comparator_2 (
    .a(subtractor_1_out), .b(12'h1f), .gt(comparator_2_gt));  // open: eq, lt
  Multiplexer #(.width(5), .enable("false")) multiplexer_3 (
    .in0(subtractor_1_out[4:0]), .in1({5{1'b1}}), .out(M), .sel(comparator_2_gt));
  Subtractor #(.width(12)) subtractor_1 (.a(N), .b(multiplexer_2_out), .out(subtractor_1_out));  // open: bin, bout

  // Notes on the sheet:
  //   Comparating A's Exponent with B's
  //   Bigger Exponent
  //   Smaller Exponent
endmodule

module Significand_Compare (
  input  [18:0] A,
  input  [18:0] B,
  input  S,
  output greater,
  output Less,
  output Equals,
  output [18:0] O1,
  output [18:0] O2
);

  Comparator #(.width(19), .mode("unsigned")) comparator_1 (.a(B), .b(A), .gt(greater), .eq(Equals), .lt(Less));
  Multiplexer #(.width(19), .enable("false")) multiplexer_1 (.in0(B), .in1(A), .out(O1), .sel(S));
  Multiplexer #(.width(19), .enable("false")) multiplexer_2 (.in0(A), .in1(B), .out(O2), .sel(S));
endmodule

// MAIN
module Main (
  input  [31:0] A,
  input  [31:0] B,
  output [31:0] S,
  output Overflow,
  output Underflow
);

  wire Exponent_Compare_k, Exponent_Compare_s, Exponent_Compare_s_prime, n7486_1_p3, Rounding_output,
       Significand_Compare_equals, Significand_Compare_greater;
  wire [0:0] Sign_Bit_s;
  wire [4:0] Exponent_Compare_m;
  wire [11:0] Exponent_Compare_n, Normalize_final_exponent, Normalize_for_rounding,
       Truncate_Roundup_resultant_exp;
  wire [18:0] Significand_Compare_o1, Significand_Compare_o2, Truncate_Roundup_resultant_signif;
  wire [30:0] Normalize_significant, Shifting___Adding_Significands_final_significant,
       Shifting___Adding_Significands_s_2;

  // _7486 7486_1: pin names not known; wires that end beside it: A[31], B[31], n7486_1_p3
  Exponent_Compare Exponent_Compare (
    .A(A[30:19]), .M(Exponent_Compare_m), .K(Exponent_Compare_k), .S(Exponent_Compare_s), .B(B[30:19]),
    .S_prime(Exponent_Compare_s_prime), .N(Exponent_Compare_n));
  Sign_Bit Sign_Bit (
    .IO_M1(Shifting___Adding_Significands_s_2[30]), .Sign_Bit_of_A(A[31]), .Sign_Bit_of_B(B[31]),
    .greater(Significand_Compare_greater), .S_Exponent_Comp(Exponent_Compare_s),
    .Selection_Bit__1Y_of_7486(n7486_1_p3), .S_prime__Exponent_Comp(Exponent_Compare_s_prime),
    .S(Sign_Bit_s[0]), .SIGN_bIT_OF_S(S[31]));
  Significand_Compare Significand_Compare (
    .S(Exponent_Compare_k), .A(A[18:0]), .B(B[18:0]), .greater(Significand_Compare_greater),
    .Equals(Significand_Compare_equals), .O1(Significand_Compare_o1), .O2(Significand_Compare_o2));  // open: Less
  Shifting___Adding_Signifcands Shifting___Adding_Significands (
    .O1(Significand_Compare_o1), .O2(Significand_Compare_o2), .MM(Exponent_Compare_m), .S(n7486_1_p3),
    .B(Sign_Bit_s[0]), .S_2(Shifting___Adding_Significands_s_2),
    .Final_Significant(Shifting___Adding_Significands_final_significant));
  Zero_handling zero_Handling (
    .Significand_Compare(Significand_Compare_equals), .Exponent_Compare(Exponent_Compare_s),
    .XOR_of_sign_bits(n7486_1_p3), .Resultant_Exponent(Truncate_Roundup_resultant_exp), .Exponent(S[30:19]),
    .Resultant_Significand(Truncate_Roundup_resultant_signif), .Fraction(S[18:0]));
  Normalize Normalize (
    .A(Shifting___Adding_Significands_final_significant), .B({{11{1'b0}}, Sign_Bit_s[0]}),
    .N__Exponent_Compare(Exponent_Compare_n), .Significant(Normalize_significant), .Overflow(Overflow),
    .Final_Exponent(Normalize_final_exponent), .For_Rounding(Normalize_for_rounding));  // open: For_Left_Shift
  Rounding Rounding (
    .R(Normalize_significant[8]), .G(Normalize_significant[9]), .S_0_7(Normalize_significant[7:0]),
    .LSB_10(Normalize_significant[10]), .Output(Rounding_output));
  Underflow u_Underflow (
    .XOR_of_sign_bits(n7486_1_p3), .Subtrahend_of_Big_Exponent(Normalize_for_rounding),
    .Big_Exponent(Exponent_Compare_n), .Underflow(Underflow));
  Truncate_RoundUp Truncate_Roundup (
    .Final_exponent_Normalize(Normalize_final_exponent), .Output_Rounding(Rounding_output),
    .A(Normalize_significant[29:10]), .Resultant_Exp(Truncate_Roundup_resultant_exp),
    .Resultant_Signif(Truncate_Roundup_resultant_signif));

  // Notes on the sheet:
  //   Resultant Exponent
  //   Resultant Signficand
endmodule

module Shifting___Adding_Signifcands (
  input  [18:0] O1,
  input  [18:0] O2,
  input  [4:0] MM,
  input  S,
  input  B,
  output [30:0] S_2,
  output [30:0] Final_Significant
);

  wire [30:0] multiplexer_1_out, negator_1_out, shifter_1_out;

  Shifter #(.width(31), .shift("lr")) shifter_1 (.in({2'b01, O2, {10{1'b0}}}), .\dist (MM), .out(shifter_1_out));
  Negator #(.width(31)) negator_1 (.in(shifter_1_out), .out(negator_1_out));
  Multiplexer #(.width(31), .enable("false")) multiplexer_1 (
    .in0(shifter_1_out), .in1(negator_1_out), .out(multiplexer_1_out), .sel(S));
  Adder #(.width(31)) adder_1 (.a({2'b01, O1, {10{1'b0}}}), .b(multiplexer_1_out), .out(S_2));  // open: cin, cout
  Shifter #(.width(31), .shift("lr")) shifter_2 (.in(S_2), .\dist ({4'b0000, B}), .out(Final_Significant));

  // Notes on the sheet:
  //   diff betn significands
  //   Larger significand
  //   smaller significand
  //   shifting smaller significand 
  //   Adding significands
endmodule

module Normalize (
  input  [30:0] A,
  input  [11:0] B,
  input  [11:0] N__Exponent_Compare,
  output [30:0] Significant,
  output Overflow,
  output [4:0] For_Left_Shift,
  output [11:0] Final_Exponent,
  output [11:0] For_Rounding
);

  wire [4:0] bitfinder_1_index;

  BitFinder #(.width(31), .\type ("high1")) bitfinder_1 (.in(A), .index(bitfinder_1_index));  // open: found
  Subtractor #(.width(12)) subtractor_1 (
    .a({{7{1'b0}}, For_Left_Shift}), .b(B), .out(For_Rounding));  // open: bin, bout
  Subtractor #(.width(5)) subtractor_2 (.a(5'b11101), .b(bitfinder_1_index), .out(For_Left_Shift));  // open: bin, bout
  Subtractor #(.width(12)) subtractor_3 (
    .a(N__Exponent_Compare), .b(For_Rounding), .out(Final_Exponent));  // open: bin, bout
  Shifter #(.width(31)) shifter_1 (.in(A), .\dist (For_Left_Shift), .out(Significant));
  Comparator #(.width(12), .mode("unsigned")) comparator_1 (
    .a({12{1'b1}}), .b(Final_Exponent), .eq(Overflow));  // open: gt, lt

  // Notes on the sheet:
  //   Finding 1st one to normalize
  //   Subtracting from 29 to det shifting after finding the 1st 1 to normalize
endmodule

module I_O (
  input  [31:0] A,
  input  [31:0] B,
  output [31:0] S,
  output Overflow,
  output Underrflow
);

  Main main_1 (.A(A), .B(B), .S(S), .Overflow(Overflow), .Underflow(Underrflow));
endmodule

module Sign_Bit (
  input  IO_M1,
  input  Sign_Bit_of_A,
  input  Sign_Bit_of_B,
  input  greater,
  input  S_Exponent_Comp,
  input  Selection_Bit__1Y_of_7486,
  input  S_prime__Exponent_Comp,
  output S,
  output SIGN_bIT_OF_S
);

  wire multiplexer_2_out, n7408_1_p3, n7432_1_p3;

  // _7408 7408_1: pin names not known; wires that end beside it: greater, S_Exponent_Comp, n7408_1_p3
  // _7432 7432_1: pin names not known; wires that end beside it: n7408_1_p3, S_prime__Exponent_Comp, n7432_1_p3
  Multiplexer #(.enable("false")) multiplexer_1 (.in0(IO_M1), .in1(1'b0), .out(S), .sel(Selection_Bit__1Y_of_7486));
  Multiplexer #(.enable("false")) multiplexer_2 (
    .in0(Sign_Bit_of_A), .in1(Sign_Bit_of_B), .out(multiplexer_2_out), .sel(n7432_1_p3));
  Multiplexer #(.enable("false")) multiplexer_3 (
    .in0(Sign_Bit_of_A), .in1(multiplexer_2_out), .out(SIGN_bIT_OF_S), .sel(Selection_Bit__1Y_of_7486));

  // Notes on the sheet:
  //   Sign bit calculation
endmodule

module Rounding (
  input  R,
  input  G,
  input  [7:0] S_0_7,
  input  LSB_10,
  output Output
);

  wire n7404_1_p1, n7404_1_p2, n7404_1_p4, n7408_1_p5, n7408_1_p6, n7408_1_p9, n7408_1_p11, n7408_1_p12;

  // _7404 7404_1: pin names not known; wires that end beside it: n7404_1_p1, n7404_1_p2, R, n7404_1_p4
  // _7408 7408_1: pin names not known; wires that end beside it: G, n7404_1_p4, n7404_1_p2, LSB_10, n7408_1_p5, n7408_1_p6, n7408_1_p5, G, n7408_1_p9, n7404_1_p1, n7408_1_p11, n7408_1_p12
  BitFinder bitfinder_1 (.in(S_0_7), .found(n7404_1_p1));  // open: index
  // _7432 7432_1: pin names not known; wires that end beside it: n7408_1_p6, R, n7408_1_p9, n7408_1_p11, n7408_1_p12, Output
endmodule

module Truncate_RoundUp (
  input  [11:0] Final_exponent_Normalize,
  input  Output_Rounding,
  input  [19:0] A,
  output [11:0] Resultant_Exp,
  output [18:0] Resultant_Signif
);

  wire [20:0] adder_1_out;
  wire [20:19] shifter_1_out;

  Adder #(.width(21)) adder_1 (.a({1'b0, A}), .b({{20{1'b0}}, Output_Rounding}), .out(adder_1_out));  // open: cin, cout
  Adder #(.width(12)) adder_2 (
    .a(Final_exponent_Normalize), .b({{11{1'b0}}, adder_1_out[20]}), .out(Resultant_Exp));  // open: cin, cout
  Shifter #(.width(21), .shift("lr")) shifter_1 (
    .in(adder_1_out), .\dist ({4'b0000, adder_1_out[20]}), .out({shifter_1_out, Resultant_Signif}));
endmodule

module Underflow (
  input  [11:0] Subtrahend_of_Big_Exponent,
  input  [11:0] Big_Exponent,
  input  XOR_of_sign_bits,
  output Underflow
);

  wire comparator_1_eq, comparator_1_lt, n7432_1_p3;

  Comparator #(.width(12), .mode("unsigned")) comparator_1 (
    .a(Big_Exponent), .b(Subtrahend_of_Big_Exponent), .eq(comparator_1_eq), .lt(comparator_1_lt));  // open: gt
  // _7432 7432_1: pin names not known; wires that end beside it: comparator_1_eq, comparator_1_lt, n7432_1_p3
  // _7408 7408_1: pin names not known; wires that end beside it: n7432_1_p3, XOR_of_sign_bits, Underflow
endmodule

module Zero_handling (
  input  [18:0] Resultant_Significand,
  input  [11:0] Resultant_Exponent,
  input  Significand_Compare,
  input  Exponent_Compare,
  input  XOR_of_sign_bits,
  output [11:0] Exponent,
  output [18:0] Fraction
);

  wire n7408_1_p3, n7408_1_p6;

  // _7408 7408_1: pin names not known; wires that end beside it: Significand_Compare, Exponent_Compare, n7408_1_p3, n7408_1_p3, XOR_of_sign_bits, n7408_1_p6
  Multiplexer #(.width(12)) multiplexer_1 (
    .in0(Resultant_Exponent), .in1({12{1'b0}}), .out(Exponent), .sel(n7408_1_p6));  // open: en
  Multiplexer #(.width(19)) multiplexer_2 (
    .in0(Resultant_Significand), .in1({19{1'b0}}), .out(Fraction), .sel(n7408_1_p6));  // open: en
endmodule
